# Fritzing sketch arduino-nano-oled-i2c (saved by Fritzing 0.9.5d)
breadboards: 1

parts:
  Part1 = Arduino Nano 33 BLE Sense
  o1 = Module display OLED I2C 128x64 SSD1306 [package=THT]
  S2 = Momentary Switch [package=ksa_sealed_tac_switch]
  S3 = Momentary Switch [package=ksa_sealed_tac_switch]
  S4 = Momentary Switch [package=ksa_sealed_tac_switch]
  S5 = Momentary Switch [package=ksa_sealed_tac_switch]
  R1 = Resistor [tolerance=±5% resistance=220 package="0402 [SMD]"]
  R2 = Resistor [tolerance=±5% resistance=220 package="0402 [SMD]"]
  R3 = Resistor [tolerance=±5% resistance=220 package="0402 [SMD]"]
  R4 = Resistor [tolerance=±5% resistance=220 package="0402 [SMD]"]

nets:
  GND: Part1.GND, Part1.A7, o1.GND, R1.Pin_0, R2.Pin_0, R3.Pin_0, R4.Pin_0
  N1: Part1.D4, S3.3, R1.Pin_1
  N2: Part1.D5~, S2.3, R2.Pin_1
  N3: Part1.D6~, S4.3, R3.Pin_1
  N4: Part1.D7, S5.3, R4.Pin_1
  N5: Part1.D11/MOSI, Part1.+5V
  N6: Part1.A5, o1.SCL
  N7: Part1.A4, o1.SDA
  3V3: Part1.3V3, o1.VCC, S2.1, S3.1, S4.1, S5.1

custom parts:
  Arduino Nano 33 BLE Sense: The Nano 33 BLE Sense (without headers) is Arduino’s 3.3V AI enabled board in the smallest available form factor: 45x18mm! The Arduino Nano 33 BLE Sense is a completely new board on a well-known form factor. It comes with a series of embedded sensors: 9 axis inertial sensor: what makes this board ideal for wearable devices humidity, and temperature sensor: to get highly accurate measurements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
  Module display OLED I2C 128x64 SSD1306: Ecran OLED I2C SSD163 de 128x64 avec connexion I2C
