# Fritzing sketch arduino-nano-oled-spi (saved by Fritzing 0.9.5d)
breadboards: 1

parts:
  S2 = Momentary Switch [package=ksa_sealed_tac_switch]
  S3 = Momentary Switch [package=ksa_sealed_tac_switch]
  S4 = Momentary Switch [package=ksa_sealed_tac_switch]
  S5 = Momentary Switch [package=ksa_sealed_tac_switch]
  R1 = Resistor [tolerance=±5% resistance=220 package="0402 [SMD]"]
  R2 = Resistor [tolerance=±5% resistance=220 package="0402 [SMD]"]
  R3 = Resistor [tolerance=±5% resistance=220 package="0402 [SMD]"]
  R4 = Resistor [tolerance=±5% resistance=220 package="0402 [SMD]"]
  Part2 = SPI OLED Monochrome 128x64 0.96 inch
  Part3 = Arduino Nano RP2040

nets:
  VDD: S2.1, S3.1, S4.1, S5.1, Part2.VDD, Part3.3V3
  N1: S2.3, R2.Pin_1, Part3.D5~
  N2: S3.3, R1.Pin_1, Part3.D4
  N3: S4.3, R3.Pin_1, Part3.D6~
  N4: S5.3, R4.Pin_1, Part3.D7
  GND: R1.Pin_0, R2.Pin_0, R3.Pin_0, R4.Pin_0, Part2.GND, Part2.SCK, Part2.CS, Part3.GND, Part3.D13~
  N5: Part2.SDA, Part3.D12~/MISO
  N6: Part2.RES, Part3.D8
  N7: Part2.DC, Part3.D9~
  N8: Part3.RESET, Part3.A7
  N9: Part3.D11/MOSI, Part3.+5V

custom parts:
  SPI OLED Monochrome 128x64 0.96 inch: Unknown 128x64 0.96 inch 128x64 SPI Monochrome OLED display
  Arduino Nano RP2040: At the core of the Arduino Nano RP2040 Connect is the Raspberry Pi RP2040; a dual-core Arm Cortex M0+ processor, with the on-board ESP32 being available as a co-processor. There’s 16MB of flash memory that’s off-chip, providing plenty of room for code and storage. The highly adaptable u-blox NINA-W102 WiFi and Bluetooth radio module provides connectivity, allowing the device to harness the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
