# Fritzing sketch pico-oled-i2c (saved by Fritzing 0.9.5d)
breadboards: 1

parts:
  S2 = Momentary Switch [package=ksa_sealed_tac_switch]
  S3 = Momentary Switch [package=ksa_sealed_tac_switch]
  S4 = Momentary Switch [package=ksa_sealed_tac_switch]
  S5 = Momentary Switch [package=ksa_sealed_tac_switch]
  R2 = Resistor [tolerance=±5% resistance=220 package="0402 [SMD]"]
  R3 = Resistor [tolerance=±5% resistance=220 package="0402 [SMD]"]
  R4 = Resistor [tolerance=±5% resistance=220 package="0402 [SMD]"]
  Mod1 = Raspberry Pi Pico
  R5 = Resistor [tolerance=±5% resistance=220 package="0402 [SMD]"]
  o1 = Module display OLED I2C 128x64 SSD1306 [package=THT]

nets:
  N1: S2.1, S3.1, S4.1, S5.1, o1.VCC
  N2: S2.3, R2.Pin_1, Mod1.pin_22
  N3: S3.3, Mod1.pin_21, R5.Pin_1
  N4: S4.3, R3.Pin_1, Mod1.pin_24
  N5: S5.3, R4.Pin_1, Mod1.pin_25
  N6: R2.Pin_0, R3.Pin_0, R4.Pin_0, R5.Pin_0, o1.GND
  N7: Mod1.pin_3, Mod1.pin_8, Mod1.pin_13, Mod1.pin_18, Mod1.pin_23, Mod1.pin_28, Mod1.pin_33, Mod1.pin_38
  N8: Mod1.pin_11, o1.SDA
  N9: Mod1.pin_12, o1.SCL

custom parts:
  Raspberry Pi Pico: Raspberry Pi Pico. Based around the RP2040 microcontroller the Pico is a low cost microcontroller device bringing Raspberry Pi quality, cost, and easy of use to the microcontroller space. Jan 2021, Split part in to two versions: tht (this one) and SMD. This one will drill holes for a .1 in header in pcb to allow plugging in the module as well as providing pads to solder the module to the top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
  Module display OLED I2C 128x64 SSD1306: Ecran OLED I2C SSD163 de 128x64 avec connexion I2C
