# Fritzing sketch pico-oled-spi (saved by Fritzing 0.9.5d)
breadboards: 1

parts:
  S2 = Momentary Switch [package=ksa_sealed_tac_switch]
  S3 = Momentary Switch [package=ksa_sealed_tac_switch]
  S4 = Momentary Switch [package=ksa_sealed_tac_switch]
  S5 = Momentary Switch [package=ksa_sealed_tac_switch]
  R2 = Resistor [tolerance=±5% resistance=220 package="0402 [SMD]"]
  R3 = Resistor [tolerance=±5% resistance=220 package="0402 [SMD]"]
  R4 = Resistor [tolerance=±5% resistance=220 package="0402 [SMD]"]
  Part2 = SPI OLED Monochrome 128x64 0.96 inch
  Mod1 = Raspberry Pi Pico
  R5 = Resistor [tolerance=±5% resistance=220 package="0402 [SMD]"]

nets:
  N1: S2.1, S3.1, S4.1, S5.1, Part2.VDD
  N2: S2.3, R2.Pin_1, Mod1.pin_22
  N3: S3.3, Mod1.pin_21, R5.Pin_1
  N4: S4.3, R3.Pin_1, Mod1.pin_24
  N5: S5.3, R4.Pin_1, Mod1.pin_25
  N6: R2.Pin_0, R3.Pin_0, R4.Pin_0, Part2.GND, Part2.CS, R5.Pin_0
  N7: Part2.SCK, Mod1.pin_9
  N8: Part2.SDA, Mod1.pin_10
  N9: Part2.RES, Mod1.pin_26
  N10: Part2.DC, Mod1.pin_27
  N11: Mod1.pin_3, Mod1.pin_8, Mod1.pin_13, Mod1.pin_18, Mod1.pin_23, Mod1.pin_28, Mod1.pin_33, Mod1.pin_38

custom parts:
  SPI OLED Monochrome 128x64 0.96 inch: Unknown 128x64 0.96 inch 128x64 SPI Monochrome OLED display
  Raspberry Pi Pico: Raspberry Pi Pico. Based around the RP2040 microcontroller the Pico is a low cost microcontroller device bringing Raspberry Pi quality, cost, and easy of use to the microcontroller space. Jan 2021, Split part in to two versions: tht (this one) and SMD. This one will drill holes for a .1 in header in pcb to allow plugging in the module as well as providing pads to solder the module to the top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
